# Fritzing sketch Motorcompartiment (saved by Fritzing 0.9.3b)
breadboards: 1

parts:
  Part1 = Arduino Uno (Rev3)
  Part2 = Arduino Mega 2560 (Rev3)
  Matrix_keypad1 = KEYPAD 4x4
  X1 = X113647 Stepper Driver Board [package=board]
  MOTOR1 = 28BYJ-48 Stepper Motor
  Power_plug1 = Power plug
  7_Segment9 = 7 Segment Display
  IC2 = SHIFT REGISTER [package=dil16]
  R17 = Resistor [tolerance=±5% resistance=220 package=THT]
  R18 = Resistor [tolerance=±5% resistance=220 package=THT]
  R19 = Resistor [tolerance=±5% resistance=220 package=THT]
  R20 = Resistor [tolerance=±5% resistance=220 package=THT]
  R21 = Resistor [tolerance=±5% resistance=220 package=THT]
  R22 = Resistor [tolerance=±5% resistance=220 package=THT]
  R23 = Resistor [tolerance=±5% resistance=220 package=THT]

nets:
  N1: Part1.A4/SDA, Part2.D20/SDA, Part2.SDA
  N2: Part1.A5/SCL, Part2.D21/SCL, Part2.SCL
  5V: Part1.5V, Part2.5V, IC2.SCL, IC2.VCC
  GND: Part1.GND, Part2.GND, X1.GND, Power_plug1.GND, 7_Segment9.common_cathode, IC2.GND, IC2.G
  N3: Part2.D12_PWM, IC2.RCK
  N4: Part2.D11_PWM, IC2.SER
  N5: Part2.D8_PWM, IC2.SCK
  VIN: Part2.VIN, X1.+V, Power_plug1.VCC
  N6: Part2.D2_PWM, X1.IN1
  N7: Part2.D3_PWM, X1.IN2
  N8: Part2.D4_PWM, X1.IN3
  N9: Part2.D5_PWM, X1.IN4
  N10: Part2.D27, Matrix_keypad1.col1
  N11: Part2.D29, Matrix_keypad1.col2
  N12: Part2.D31, Matrix_keypad1.col3
  N13: Part2.D33, Matrix_keypad1.col4
  N14: Part2.D35, Matrix_keypad1.row1
  N15: Part2.D37, Matrix_keypad1.row2
  N16: Part2.D39, Matrix_keypad1.row3
  N17: Part2.D41, Matrix_keypad1.row4
  N18: X1.BLUE, MOTOR1.BLUE
  N19: X1.PINK, MOTOR1.PINK
  N20: X1.YELLOW, MOTOR1.RED
  N21: X1.ORANGE, MOTOR1.ORANGE
  N22: X1.RED, MOTOR1.YELLOW
  N23: 7_Segment9.Segment_E, R18.Pin_1
  N24: 7_Segment9.Segment_D, R19.Pin_1
  N25: 7_Segment9.Segment_C, R20.Pin_1
  N26: 7_Segment9.Segment_B, R21.Pin_1
  N27: 7_Segment9.Segment_A, R23.Pin_1
  N28: 7_Segment9.Segment_F, R17.Pin_1
  N29: 7_Segment9.Segment_G, R22.Pin_1
  N30: IC2.QB, R23.Pin_0
  N31: IC2.QC, R21.Pin_0
  N32: IC2.QD, R20.Pin_0
  N33: IC2.QE, R19.Pin_0
  N34: IC2.QF, R18.Pin_0
  N35: IC2.QG, R22.Pin_0
  N36: IC2.QH, R17.Pin_0

custom parts:
  KEYPAD 4x4: Matrix keypad 16 buttons, 4 rows x 4 columns
  X113647 Stepper Driver Board: A common stepper motor driver board based on ULN2003APG darlington array
  28BYJ-48 Stepper Motor: 28BYJ-48 gear-reduction stepper motor (small)
