# Fritzing sketch Verdieping (saved by Fritzing 0.9.3b)
breadboards: 1

parts:
  Part1 = Arduino Uno (Rev3)
  IC1 = SHIFT REGISTER [package=dil16]
  R1 = Resistor [tolerance=±5% resistance=220 package=THT]
  R4 = Resistor [tolerance=±5% resistance=220 package=THT]
  R5 = Resistor [tolerance=±5% resistance=220 package=THT]
  R6 = Resistor [tolerance=±5% resistance=220 package=THT]
  R7 = Resistor [tolerance=±5% resistance=220 package=THT]
  S1 = Reed switch [package=THT]
  R9 = Resistor [tolerance=±5% resistance=220 package=THT]
  S2 = Pushbutton [package="[THT]"]
  S3 = Pushbutton [package="[THT]"]
  LED1 = LED - 5mm [color="Red (633nm)" package="5 mm [THT]"]
  R12 = Resistor [tolerance=±5% resistance=220 package=THT]
  LED2 = LED - 5mm [color="Red (633nm)" package="5 mm [THT]"]
  7_Segment8 = 7 Segment Display
  R3 = Resistor [tolerance=±5% resistance=220 package=THT]
  R8 = Resistor [tolerance=±5% resistance=220 package=THT]
  R13 = Resistor [tolerance=±5% resistance=220 package=THT]
  LED3 = LED - 5mm [color="Red (633nm)" package="5 mm [THT]"]
  Part2 = Arduino Mega 2560 (Rev3)

nets:
  N1: Part1.A4/SDA, Part2.D20/SDA, Part2.SDA
  N2: Part1.A5/SCL, Part2.D21/SCL
  N3: Part1.D8, IC1.SCK
  N4: Part1.D11_PWM/MOSI, IC1.SER
  N5: Part1.D12/MISO, IC1.RCK
  N6: Part1.D13/SCK, R13.Pin_0
  GND: Part1.GND, IC1.GND, IC1.G, S1.pin_2, R9.Pin_1, S2.Pin_1, S2.Pin_2, S3.Pin_1, S3.Pin_2, R12.Pin_1, 7_Segment8.common_cathode, LED3.cathode, Part2.GND
  N7: Part1.D2, S1.pin_1
  N8: Part1.D3_PWM, S2.Pin_3, S2.Pin_4
  N9: Part1.D4, S3.Pin_3, S3.Pin_4
  N10: Part1.D5_PWM, LED1.anode
  N11: Part1.D6_PWM, LED2.anode
  5V: Part1.5V, IC1.SCL, IC1.VCC, Part2.5V
  N12: IC1.QB, R1.Pin_0
  N13: IC1.QC, R4.Pin_0
  N14: IC1.QD, R5.Pin_0
  N15: IC1.QE, R6.Pin_0
  N16: IC1.QF, R7.Pin_0
  N17: IC1.QG, R3.Pin_0
  N18: IC1.QH, R8.Pin_0
  N19: R1.Pin_1, 7_Segment8.Segment_A
  N20: R4.Pin_1, 7_Segment8.Segment_B
  N21: R5.Pin_1, 7_Segment8.Segment_C
  N22: R6.Pin_1, 7_Segment8.Segment_D
  N23: R7.Pin_1, 7_Segment8.Segment_E
  N24: R9.Pin_0, LED1.cathode
  N25: R12.Pin_0, LED2.cathode
  N26: 7_Segment8.Segment_F, R8.Pin_1
  N27: 7_Segment8.Segment_G, R3.Pin_1
  N28: R13.Pin_1, LED3.anode

// code stored in the sketch: 7SegmentDisplay.ino
const int latchPin = 12; //Pin connected to ST_CP of 74HC595
const int clockPin = 8; //Pin connected to SH_CP of 74HC595 
const int dataPin = 11; //Pin connected to DS of 74HC595 
/*=======================================================================================================
//display 0,1,2,3,4,5,6,7,8
Number 0 :  00000011     3 
Number 1 :  10101111     159 
Number 2 :  00100101     37
Number 3 :  00001101     13
Number 4 :  10011001     153
Number 5 :  01001001     73
Number 6 :  01000001     65
Number 7 :  00011111     31
Number 8 :  00000001     1

To display the dot, simply subtract 1.
example : 1 - 1 = 0  or b0000000 0x0 to display 8
*/
/*In order to display zero your array has decimal number 3. However using the shift register
it is actuall the binary number that is uploaded into the resitsre: zie the table above for zero: 00000011. 
*/
//int datArray[9] = {3, 159, 37, 13, 153, 73, 65, 31, 1}; // array without the decimal
byte datArray[10] = {252, 96, 218, 242, 102, 182, 190, 224, 254, 246}; // array without the decimal

//int datArray[9] = {0, 1, 3, 7, 15, 31, 63, 127, 255}; // array without the decimal
//int datArray[10] = {128, 64, 32, 16, 8, 4}; // array without the decimal

byte state = 0;



const byte reedPin = 2;
boolean reedState = false;

const byte buttonDownPin = 3;
boolean buttonDownState = false;
const byte buttonUpPin = 4;
boolean buttonUpState = false;
const byte ledDownPin = 5;
const byte ledUpPin = 6;



void setup ()
{
  //set pins to output

  pinMode(latchPin, OUTPUT);
  pinMode(clockPin, OUTPUT);
  pinMode(dataPin, OUTPUT);

  pinMode(reedPin, INPUT_PULLUP);

  pinMode(buttonDownPin, INPUT_PULLUP);
  pinMode(buttonUpPin, INPUT_PULLUP);
  pinMode(ledDownPin, OUTPUT);
  pinMode(ledUpPin, OUTPUT);

  digitalWrite(latchPin, LOW);
  shiftOut(dataPin, clockPin, LSBFIRST, datArray[state]);
  digitalWrite(latchPin, HIGH);
}


void loop()
{
	/*
  //loop from 0 to 9
  for(int num = 0; num < 10; num++)
  {
    digitalWrite(latchPin, LOW);
    shiftOut(dataPin, clockPin, LSBFIRST, datArray[num]);
    digitalWrite(latchPin, HIGH);
    delay(1000); //wait for a second
  }
	*/


  if (!digitalRead(reedPin)){
    if (!reedState){
      reedState = true;
      // Set value
      state = 0;
      digitalWrite(latchPin, LOW);
      shiftOut(dataPin, clockPin, LSBFIRST, datArray[0]);
      digitalWrite(latchPin, HIGH);
    }
  } else {
    reedState = false;
  }
  
	if (!digitalRead(buttonDownPin)){
		if (!buttonDownState){
			buttonDownState = true;
			// Count down
			if (state > 0){
				digitalWrite(latchPin, LOW);
    		shiftOut(dataPin, clockPin, LSBFIRST, datArray[--state]);
    		digitalWrite(latchPin, HIGH);
			}
		}
	} else {
		buttonDownState = false;
	}

	if (!digitalRead(buttonUpPin)){
		if (!buttonUpState){
			buttonUpState = true;
			// Count up
			if (state < 9){
				digitalWrite(latchPin, LOW);
    		shiftOut(dataPin, clockPin, LSBFIRST, datArray[++state]);
    		digitalWrite(latchPin, HIGH);
			}
		}
	} else {
		buttonUpState = false;
	}
	

	digitalWrite(ledDownPin, !digitalRead(buttonDownPin));
	digitalWrite(ledUpPin, !digitalRead(buttonUpPin));
}
